// Logisim project atividade fixa.circ as structural Verilog: 4 circuits, main circuit half adder
module half_adder (
  input  a,
  input  b,
  output carry_in,
  output s
);

  and and_1 (carry_in, a, b);
  xor xor_1 (s, a, b);
endmodule

module full_adder (
  input  A,
  input  B,
  input  carry_in,
  output carry_out,
  output S
);

  wire and_1_out, and_2_out, xor_1_out;

  and and_1 (and_1_out, A, B);
  xor xor_1 (xor_1_out, A, B);
  and and_2 (and_2_out, carry_in, xor_1_out);
  xor xor_2 (S, carry_in, xor_1_out);
  or or_1 (carry_out, and_1_out, and_2_out);
endmodule

module somador_mutiplos_bits (
  input  b3,
  input  b2,
  input  b1,
  input  b0,
  input  a3,
  input  a2,
  input  a1,
  input  a0,
  input  carry_in,
  output carry_out,
  output S3,
  output S2,
  output S1,
  output S0
);

  wire full_adder_0_carry_out, full_adder_1_carry_out, full_adder_2_carry_out;

  full_adder full_adder_0 (.A(b0), .B(a0), .carry_out(full_adder_0_carry_out), .carry_in(carry_in), .S(S0));
  full_adder full_adder_1 (
    .A(b1), .B(a1), .carry_out(full_adder_1_carry_out), .carry_in(full_adder_0_carry_out), .S(S1));
  full_adder full_adder_2 (
    .A(b2), .B(a2), .carry_out(full_adder_2_carry_out), .carry_in(full_adder_1_carry_out), .S(S2));
  full_adder full_adder_3 (.A(b3), .B(a3), .carry_out(carry_out), .carry_in(full_adder_2_carry_out), .S(S3));
endmodule

module somador_8bits (
  input  in_1,
  input  in_2,
  input  in_3,
  input  in_4,
  input  in_5,
  input  in_6,
  input  in_7,
  input  in_8,
  input  in_9,
  input  in_10,
  input  in_11,
  input  in_12,
  input  in_13,
  input  in_14,
  input  in_15,
  input  in_16
);
endmodule
