// Logisim project logisim 1.circ as structural Verilog: 1 circuit, main circuit main
module main (
  input  A,
  input  B,
  input  a_2,
  input  C
);

  wire and_1_out, not_1_out, or_1_out, or_2_out;

  not not_1 (not_1_out, B);
  or or_1 (or_1_out, A, B);
  or or_2 (or_2_out, not_1_out, C);
  and and_1 (and_1_out, or_1_out, or_2_out);
endmodule
